# Fritzing sketch diagram (saved by Fritzing 0.9.3b)
breadboards: 1

parts:
  Part1 = Arduino Mega ADK (Rev3)
  LED2 = smd LED [color="Red (633nm)" package="0805 [SMD]"]
  S2 = Toggle Switch [package=THT]

nets:
  N1: Part1.A0, LED2.anode, S2.COM
  N2: Part1.GND, LED2.cathode, S2.L1
  N3: Part1.5V, S2.L2
